// Logisim project MPMPcpu_phase11.circ as structural Verilog: 4 circuits, main circuit main
module main (
  input  in_1
);

  wire and_1_out, and_3_out, and_5_out, and_6_out, and_9_out, CARRY_FLAG, CLK, comparator_1_eq,
       CTRL_ALU_ENABLE_PASSING, CTRL_ALU_PASS_Y_INSTEAD, CTRL_ALU_WE, CTRL_ENABLE_FLAG_EXPECTATION,
       CTRL_FLAG_EXPECTED_VALUE, CTRL_INCREMENT_PC_AND_FINISH, CTRL_IO_WE, CTRL_RAM_WE,
       CTRL_REG_A_IS_REG_RES, CTRL_RF_FORCE_WRITE_PC, CTRL_RF_INP_USE_IO, CTRL_RF_INP_USE_MEM, CTRL_RF_WE,
       CTRL_SET_IO_REG_PAGE, CTRL_SET_X_TO_IMM3_FROM_REG_RES, CTRL_WHICH_FLAG_EXPECTED, multiplexer_3_out,
       not_1_out, not_2_out, or_1_out, or_2_out, xnor_1_out, ZERO_FLAG;
  wire [2:0] REG_A, REG_B, REG_RES, rom_1_data;
  wire [3:0] ALU_OP4;
  wire [6:0] IO_READ_VAL;
  wire [6:5] and_2_out;
  wire [7:0] alu_1_result, alu_1_zf, and_7_out, and_8_out, IMM, INSTR_ADDR, INSTR_PAGE, IO_ADDR,
       multiplexer_1_out, multiplexer_2_out, multiplexer_5_out, multiplexer_7_out, or_4_out, RAM_ADDR,
       RAM_INP, RAM_OUT, registerfile_1_dbg_r2, registerfile_1_dbg_r3, registerfile_1_dbg_r4,
       registerfile_1_dbg_r5, registerfile_1_dbg_r6, registerfile_1_dbg_r7, registerfile_1_out_b,
       registerfile_1_sp, registerfile_2_dbg_r2, registerfile_2_dbg_r3, registerfile_2_dbg_r4,
       registerfile_2_dbg_r6, registerfile_2_dbg_r7, registerfile_2_pc, registerfile_2_sp, rom_2_data;
  wire [7:2] FLAGS_q;
  wire [11:3] rom_1_data_2;
  wire [15:15] CONTROL_ROM_data;

  RAM ram_1 (.addr(RAM_ADDR), .we(CTRL_RAM_WE), .oe(1'b1), .clk(CLK), .din(RAM_INP), .dout(RAM_OUT));
  // Probe on RAM_INP
  Multiplexer #(.width(8)) multiplexer_1 (
    .in0(RAM_INP), .in1(RAM_OUT), .out(multiplexer_1_out), .sel(CTRL_RF_INP_USE_MEM));
  // Probe on multiplexer_2_out
  Multiplexer #(.width(8)) multiplexer_2 (
    .in0(multiplexer_1_out), .in1({1'b0, IO_READ_VAL}), .out(multiplexer_2_out), .sel(CTRL_RF_INP_USE_IO));
  Multiplexer multiplexer_3 (
    .in0(ZERO_FLAG), .in1(CARRY_FLAG), .out(multiplexer_3_out), .sel(CTRL_WHICH_FLAG_EXPECTED));
  xnor xnor_1 (xnor_1_out, multiplexer_3_out, CTRL_FLAG_EXPECTED_VALUE);
  or or_1 (or_1_out, xnor_1_out, ~CTRL_ENABLE_FLAG_EXPECTATION);  // OR_Gate
  and and_1 (and_1_out, CTRL_RF_WE, or_1_out);
  ROM #(.addrWidth(16), .dataWidth(16)) rom_1 (
    .addr({INSTR_PAGE, INSTR_ADDR}), .data({ALU_OP4, rom_1_data_2[11], rom_1_data, rom_1_data_2[7:3], REG_B}));
  // Probe on REG_A
  // Probe on REG_B
  Pull_Resistor pull_resistor_1 (.node(REG_RES));
  assign REG_RES = not_1_out ? rom_1_data : 3'bz;  // Controlled_Buffer controlled_buffer_1
  not not_1 (not_1_out, CTRL_RF_FORCE_WRITE_PC);
  Multiplexer #(.width(3)) multiplexer_4 (.in0(rom_1_data), .in1(rom_1_data_2[5:3]), .out(REG_A), .sel(not_2_out));
  not not_2 (not_2_out, CTRL_REG_A_IS_REG_RES);
  // Probe on INSTR_ADDR
  RegisterFile registerfile_1 (
    .CLK(CLK), .RST(in_1), .WE(and_1_out), .DO_PC_INCREMENT(CTRL_INCREMENT_PC_AND_FINISH),
    .INP(multiplexer_2_out), .REG_WRITE(REG_RES), .REG_READ_A(REG_A), .REG_READ_B(REG_B), .OUT_A(RAM_ADDR),
    .OUT_B(registerfile_1_out_b), .PC(INSTR_ADDR), .SP(registerfile_1_sp), .DBG_R2(registerfile_1_dbg_r2),
    .DBG_R3(registerfile_1_dbg_r3), .DBG_R4(registerfile_1_dbg_r4), .DBG_R5(registerfile_1_dbg_r5),
    .DBG_R6(registerfile_1_dbg_r6), .DBG_R7(registerfile_1_dbg_r7));
  // Probe on INSTR_ADDR
  // Probe on registerfile_1_sp
  // Probe on registerfile_1_dbg_r2
  // Probe on registerfile_1_dbg_r3
  // Probe on registerfile_1_dbg_r4
  // Probe on registerfile_1_dbg_r5
  // Probe on registerfile_1_dbg_r6
  // Probe on registerfile_1_dbg_r7
  buf or_2 (or_2_out, in_1);  // OR_Gate
  Counter #(.max('h1), .width(1)) counter_1 (
    .load(1'b0), .count(1'b1), .Q(CTRL_INCREMENT_PC_AND_FINISH), .up(1'b1), .clk(CLK), .clr(or_2_out));  // open: D, carry
  Clock clock_1 (.out(CLK));
  and and_2 (and_2_out[5], ~rom_1_data_2[11], rom_1_data_2[6]);  // AND_Gate
  or or_3 (and_2_out[6], rom_1_data_2[11], and_3_out);
  and and_3 (and_3_out, ~rom_1_data_2[11], rom_1_data_2[7]);  // AND_Gate
  Multiplexer #(.width(8)) multiplexer_5 (
    .in0(RAM_ADDR), .in1({{5{1'b0}}, REG_RES}), .out(multiplexer_5_out), .sel(CTRL_SET_X_TO_IMM3_FROM_REG_RES));
  // Probe on multiplexer_5_out
  // Probe on IO_ADDR
  Multiplexer #(.width(8)) multiplexer_6 (.in0(registerfile_1_out_b), .in1(IMM), .out(IO_ADDR), .sel(and_2_out[6]));
  ROM #(.addrWidth(7), .dataWidth(16)) CONTROL_ROM (
    .addr({and_2_out, ALU_OP4, CTRL_INCREMENT_PC_AND_FINISH}),
    .data({CONTROL_ROM_data[15], CTRL_ALU_WE, CTRL_ALU_ENABLE_PASSING, CTRL_ALU_PASS_Y_INSTEAD, CTRL_SET_X_TO_IMM3_FROM_REG_RES, CTRL_ENABLE_FLAG_EXPECTATION, CTRL_FLAG_EXPECTED_VALUE, CTRL_WHICH_FLAG_EXPECTED, CTRL_REG_A_IS_REG_RES, CTRL_SET_IO_REG_PAGE, CTRL_RF_FORCE_WRITE_PC, CTRL_RF_INP_USE_IO, CTRL_RF_INP_USE_MEM, CTRL_IO_WE, CTRL_RAM_WE, CTRL_RF_WE}));
  Multiplexer #(.width(8)) multiplexer_7 (
    .in0(IO_ADDR), .in1(8'h5), .out(multiplexer_7_out), .sel(CTRL_SET_IO_REG_PAGE));
  assign IMM = {rom_1_data_2[7:3], REG_B} & {{5{rom_1_data_2[11]}}, 3'b111};  // AND_Gate and_4, 8 bits wide
  // Probe on IMM
  // Probe on multiplexer_7_out[2:0]
  // Probe on ALU_OP4
  and and_5 (and_5_out, ~CTRL_ALU_ENABLE_PASSING, CTRL_ALU_WE);  // AND_Gate
  and and_6 (and_6_out, CONTROL_ROM_data[15], CLK);
  RegisterFile registerfile_2 (
    .CLK(CLK), .RST(in_1), .WE(CTRL_IO_WE), .DO_PC_INCREMENT(1'b0), .INP(multiplexer_5_out),
    .REG_WRITE(multiplexer_7_out[2:0]), .REG_READ_A(multiplexer_7_out[2:0]), .PC(registerfile_2_pc),
    .SP(registerfile_2_sp), .DBG_R2(registerfile_2_dbg_r2), .DBG_R3(registerfile_2_dbg_r3),
    .DBG_R4(registerfile_2_dbg_r4), .DBG_R5(INSTR_PAGE), .DBG_R6(registerfile_2_dbg_r6),
    .DBG_R7(registerfile_2_dbg_r7));  // open: REG_READ_B, OUT_A, OUT_B
  // Probe on registerfile_2_pc
  // Probe on registerfile_2_sp
  // Probe on registerfile_2_dbg_r2
  // Probe on registerfile_2_dbg_r3
  // Probe on registerfile_2_dbg_r4
  // Probe on INSTR_PAGE
  // Probe on registerfile_2_dbg_r6
  // Probe on registerfile_2_dbg_r7
  // Probe on alu_1_result
  ALU alu_1 (
    .OP(ALU_OP4), .X(multiplexer_5_out), .Y(IO_ADDR), .CIN(CARRY_FLAG),
    .PASS_X_OR_Y(CTRL_ALU_PASS_Y_INSTEAD), .ENABLE_PASSING(CTRL_ALU_ENABLE_PASSING), .RESULT(alu_1_result),
    .ZF(alu_1_zf[0]), .OVF(alu_1_zf[2]), .EF(alu_1_zf[3]), .RF(alu_1_zf[4]), .CF(alu_1_zf[1]));
  Comparator #(.width(3)) comparator_1 (.a(3'b001), .b(multiplexer_7_out[2:0]), .eq(comparator_1_eq));  // open: gt, lt
  Register ALU_RESULT (.D(alu_1_result), .en(CTRL_ALU_WE), .clk(CLK), .Q(RAM_INP));  // open: clr
  assign and_7_out = alu_1_zf & rom_2_data;  // AND_Gate and_7, 8 bits wide
  assign and_8_out = {FLAGS_q, CARRY_FLAG, ZERO_FLAG} & ~rom_2_data;  // AND_Gate and_8, 8 bits wide
  Register FLAGS (.D(or_4_out), .en(and_5_out), .clk(CLK), .Q({FLAGS_q, CARRY_FLAG, ZERO_FLAG}), .clr(in_1));
  assign or_4_out = and_7_out | and_8_out;  // OR_Gate or_4, 8 bits wide
  ROM #(.addrWidth(4)) rom_2 (.addr(ALU_OP4), .data(rom_2_data));
  and and_9 (and_9_out, CTRL_IO_WE, comparator_1_eq);
  // RGB_Video #(.height(64), .scale(8), .width(64)) rgb_video_1: pin names not known; wires that end beside it: in_1, CLK, and_9_out, registerfile_2_pc[7:2], registerfile_2_sp[7:2], {registerfile_2_sp[1:0], registerfile_2_pc[1:0]}
  Keyboard #(.buflen(1)) keyboard_1 (
    .clk(CLK), .re(CTRL_RF_INP_USE_IO), .clr(1'b0), .data(IO_READ_VAL));  // open: avail
  Counter #(.max('hffff), .width(16)) counter_2 (
    .load(1'b0), .count(1'b1), .up(1'b1), .clk(CTRL_INCREMENT_PC_AND_FINISH), .clr(in_1));  // open: D, Q, carry

  // Other names for the same wires on the sheet: RST = in_1

  // Notes on the sheet:
  //   Data Memory
  //   contents of rom_1 (hex, n*v repeats v):
  //   8809 13dc 8824 4e4 8824 3dc 8824 14e4 8824 fb02 fc01 fa00 fd7e 8228 2d1 fd81 8228 2d1 fda5 8228 2d1
  //   fd81 8228 2d1 fd7e 8228 2d1 fd18 8228 2d1 fd7e 8228 2d1 fd24 8228 2d1 faff 2d1 4510 fe08 6f0 9825
  //   16f1 45e9 c828 43f2 a3db 44d2 a3d9 dc01 db00 53d3 9828 ef07 7f8 9824 97fe f9
  //   Instruction Memory
  //   contents of CONTROL_ROM (hex, n*v repeats v):
  //   6000 8001 6*0 6000 8009 6*0 6000 8082 6*0 6000 80e5 a011 5*0 4000 8001 4000 8001 4000 8001 4000 8001
  //   4000 8001 4000 8001 4000 8001 4000 8001 4000 8001 4000 8001 4000 8001 4000 8001 4000 8001 4000 8001
  //   4000 8001 4000 8001 16*0 7840 8021 7000 8601 7000 8701 7000 8401 7000 b501 b084 0 6000 8011 7000
  //   8001 4000 8001 4000 8001 4000 8001 4000 8001 4000 8001 4000 8001 4000 8001 4000 8001 4000 8001 4000
  //   8001 4000 8001 4000 8001 4000 8001 4000 8001 4000 8001 4000 8001
  //   Control Bit Memory
  //   contents of rom_2 (hex, n*v repeats v):
  //   7 7 5 19 3 3 1 0 0 5*1 7 7
  //   Flag Overwrite Memory
endmodule

module ALU (
  input  [3:0] OP,
  input  [7:0] X,
  input  [7:0] Y,
  input  CIN,
  input  PASS_X_OR_Y,
  input  ENABLE_PASSING,
  output [7:0] RESULT,
  output ZF,
  output OVF,
  output EF,
  output RF,
  output CF
);

  wire ADD_COUT, and_1_out, and_4_out, and_5_out, bitfinder_1_found, bitfinder_2_found, C_OP,
       comparator_1_eq, comparator_2_lt, comparator_3_lt, comparator_4_eq, comparator_5_eq, comparator_6_eq,
       comparator_7_gt, not_2_out, SUB_COUT;
  wire [2:0] bitfinder_1_index, bitfinder_2_index, multiplexer_5_out, subtractor_2_out;
  wire [2:2] not_3_out;
  wire [7:0] adder_1_out, and_2_out, DIV_REM, divider_1_out, MUL_CARRY, multiplexer_1_out, multiplexer_2_out,
       multiplier_1_out, negator_1_out, not_1_out, or_1_out, shifter_1_out, shifter_2_out, subtractor_1_out,
       xnor_1_out, xor_1_out;

  and and_1 (and_1_out, CIN, C_OP);
  Adder adder_1 (.a(X), .b(Y), .out(adder_1_out), .cin(and_1_out), .cout(ADD_COUT));
  Subtractor subtractor_1 (.a(X), .b(Y), .out(subtractor_1_out), .bin(and_1_out), .bout(SUB_COUT));
  Multiplier multiplier_1 (.a(X), .b(Y), .out(multiplier_1_out), .cout(MUL_CARRY));  // open: cin
  Divider divider_1 (.a(X), .b(Y), .out(divider_1_out), .rem(DIV_REM));  // open: upper
  Shifter shifter_1 (.in(X), .\dist (Y[2:0]), .out(shifter_1_out));
  Shifter #(.shift("lr")) shifter_2 (.in(X), .\dist (Y[2:0]), .out(shifter_2_out));
  Negator negator_1 (.in(X), .out(negator_1_out));
  assign and_2_out = X & Y;  // AND_Gate and_2, 8 bits wide
  assign or_1_out = X | Y;  // OR_Gate or_1, 8 bits wide
  assign xor_1_out = X ^ Y;  // XOR_Gate xor_1, 8 bits wide
  assign xnor_1_out = ~(X ^ Y);  // XNOR_Gate xnor_1, 8 bits wide
  assign not_1_out = ~X;  // NOT_Gate not_1, 8 bits wide
  and and_3 (C_OP, OP[1], OP[2], OP[3]);
  Multiplexer #(.select(4), .width(8)) multiplexer_1 (
    .in0(adder_1_out), .in1(subtractor_1_out), .in2(multiplier_1_out), .in3(divider_1_out),
    .in4(shifter_1_out), .in5(shifter_2_out), .in6(negator_1_out), .in9(and_2_out), .in10(or_1_out),
    .in11(xor_1_out), .in12(xnor_1_out), .in13(not_1_out), .in14(adder_1_out), .in15(subtractor_1_out),
    .out(multiplexer_1_out), .sel(OP));  // open: in7, in8
  BitFinder #(.\type ("high1")) bitfinder_1 (.in(X), .index(bitfinder_1_index), .found(bitfinder_1_found));
  BitFinder bitfinder_2 (.in(X), .index(bitfinder_2_index), .found(bitfinder_2_found));
  nor Zero_Test (ZF, multiplexer_1_out[7], multiplexer_1_out[6], multiplexer_1_out[5], multiplexer_1_out[4], multiplexer_1_out[3], multiplexer_1_out[2], multiplexer_1_out[1], multiplexer_1_out[0]);
  Subtractor #(.width(3)) subtractor_2 (.a(3'b111), .b(bitfinder_1_index), .out(subtractor_2_out));  // open: bin, bout
  Multiplexer #(.width(8)) multiplexer_2 (.in0(X), .in1(Y), .out(multiplexer_2_out), .sel(PASS_X_OR_Y));
  Multiplexer #(.width(8)) multiplexer_3 (
    .in0(multiplexer_1_out), .in1(multiplexer_2_out), .out(RESULT), .sel(ENABLE_PASSING));
  Comparator #(.mode("unsigned"), .width(4)) comparator_1 (.a(OP), .b(4'b0011), .eq(comparator_1_eq));  // open: gt, lt
  Comparator #(.mode("unsigned"), .width(3)) comparator_2 (
    .a(subtractor_2_out), .b(Y[2:0]), .lt(comparator_2_lt));  // open: gt, eq
  and and_4 (and_4_out, comparator_2_lt, bitfinder_1_found);
  Comparator #(.mode("unsigned"), .width(3)) comparator_3 (
    .a(bitfinder_2_index), .b(Y[2:0]), .lt(comparator_3_lt));  // open: gt, eq
  and and_5 (and_5_out, comparator_3_lt, bitfinder_2_found);
  Comparator #(.mode("unsigned")) comparator_4 (.a(Y), .b({8{1'b0}}), .eq(comparator_4_eq));  // open: gt, lt
  Comparator #(.mode("unsigned")) comparator_5 (.a(DIV_REM), .b({8{1'b0}}), .eq(comparator_5_eq));  // open: gt, lt
  Comparator #(.mode("unsigned"), .width(4)) comparator_6 (.a(OP), .b(4'b0010), .eq(comparator_6_eq));  // open: gt, lt
  and and_6 (OVF, comparator_6_eq, comparator_7_gt);
  Comparator #(.mode("unsigned")) comparator_7 (.a(MUL_CARRY), .b({8{1'b0}}), .gt(comparator_7_gt));  // open: eq, lt
  and and_7 (EF, comparator_4_eq, comparator_1_eq);
  and and_8 (RF, comparator_1_eq, not_2_out);
  not not_2 (not_2_out, comparator_5_eq);
  Multiplexer #(.select(3)) multiplexer_4 (
    .in0(ADD_COUT), .in1(SUB_COUT), .in4(and_4_out), .in5(and_5_out), .out(CF), .sel(multiplexer_5_out));  // open: in2, in3, in6, in7
  Multiplexer #(.width(3)) multiplexer_5 (
    .in0(OP[2:0]), .in1({not_3_out[2], 2'b00}), .out(multiplexer_5_out), .sel(C_OP));
  not not_3 (not_3_out[2], OP[0]);
  Pull_Resistor pull_resistor_1 (.node(CF));

  // Other names for the same wires on the sheet: SHIFT[2:0] = Y[2:0]

  // Notes on the sheet:
  //   TODO: Overflow Flag for Add, Sub, AddC, SubC
endmodule

module RegisterFile (
  input  CLK,
  input  RST,
  input  WE,
  input  DO_PC_INCREMENT,
  input  [7:0] INP,
  input  [2:0] REG_WRITE,
  input  [2:0] REG_READ_A,
  input  [2:0] REG_READ_B,
  output [7:0] OUT_A,
  output [7:0] OUT_B,
  output [7:0] PC,
  output [7:0] SP,
  output [7:0] DBG_R2,
  output [7:0] DBG_R3,
  output [7:0] DBG_R4,
  output [7:0] DBG_R5,
  output [7:0] DBG_R6,
  output [7:0] DBG_R7
);

  wire demultiplexer_1_out0, demultiplexer_1_out1, demultiplexer_1_out2, demultiplexer_1_out3,
       demultiplexer_1_out4, demultiplexer_1_out5, demultiplexer_1_out6, demultiplexer_1_out7, or_1_out;
  wire [2:0] multiplexer_1_out;
  wire [7:0] INP_t;

  Multiplexer #(.width(3)) multiplexer_1 (.in0(REG_WRITE), .in1(3'b001), .out(multiplexer_1_out), .sel(RST));
  or or_1 (or_1_out, WE, RST);
  Demultiplexer #(.select(3)) demultiplexer_1 (
    .out0(demultiplexer_1_out0), .out1(demultiplexer_1_out1), .out2(demultiplexer_1_out2),
    .out3(demultiplexer_1_out3), .out4(demultiplexer_1_out4), .out5(demultiplexer_1_out5),
    .out6(demultiplexer_1_out6), .out7(demultiplexer_1_out7), .in(or_1_out), .sel(multiplexer_1_out));
  Register R1 (.D(INP_t), .en(demultiplexer_1_out1), .clk(CLK), .Q(SP));  // open: clr
  Register R2 (.D(INP_t), .en(demultiplexer_1_out2), .clk(CLK), .Q(DBG_R2), .clr(RST));
  Register R3 (.D(INP_t), .en(demultiplexer_1_out3), .clk(CLK), .Q(DBG_R3), .clr(RST));
  Register R4 (.D(INP_t), .en(demultiplexer_1_out4), .clk(CLK), .Q(DBG_R4), .clr(RST));
  Register R5 (.D(INP_t), .en(demultiplexer_1_out5), .clk(CLK), .Q(DBG_R5), .clr(RST));
  Register R6 (.D(INP_t), .en(demultiplexer_1_out6), .clk(CLK), .Q(DBG_R6), .clr(RST));
  Register R7 (.D(INP_t), .en(demultiplexer_1_out7), .clk(CLK), .Q(DBG_R7), .clr(RST));
  Counter ProgramCounter (
    .load(demultiplexer_1_out0), .D(INP_t), .count(DO_PC_INCREMENT), .Q(PC), .up(1'b1), .clk(CLK), .clr(RST));  // open: carry
  Multiplexer #(.width(8)) multiplexer_2 (.in0(INP), .in1({8{1'b1}}), .out(INP_t), .sel(RST));
  Multiplexer #(.select(3), .width(8)) multiplexer_3 (
    .in0(PC), .in1(SP), .in2(DBG_R2), .in3(DBG_R3), .in4(DBG_R4), .in5(DBG_R5), .in6(DBG_R6), .in7(DBG_R7),
    .out(OUT_A), .sel(REG_READ_A));
  Multiplexer #(.select(3), .width(8)) multiplexer_4 (
    .in0(PC), .in1(SP), .in2(DBG_R2), .in3(DBG_R3), .in4(DBG_R4), .in5(DBG_R5), .in6(DBG_R6), .in7(DBG_R7),
    .out(OUT_B), .sel(REG_READ_B));

  // Notes on the sheet:
  //   REG_WRITE: initial=0x2
endmodule

module IO (
  input  CLK,
  input  RST,
  input  WE,
  input  DO_PC_INCREMENT,
  input  [7:0] INP,
  input  [2:0] REG_WRITE,
  input  [2:0] REG_READ_A,
  input  [7:0] INP_KEYBOARD,
  input  WE_KEYBOARD,
  output [7:0] SCREEN_X,
  output [7:0] OUT_A,
  output [7:0] SCREEN_Y,
  output [7:0] IO_R2,
  output [7:0] IO_R3,
  output [7:0] IO_R4,
  output [7:0] INSTR_PAGE,
  output [7:0] KEYBOARD,
  output [7:0] IO_R7
);

  wire demultiplexer_1_out0, demultiplexer_1_out1, demultiplexer_1_out2, demultiplexer_1_out3,
       demultiplexer_1_out4, demultiplexer_1_out5, demultiplexer_1_out7, or_1_out;

  or or_1 (or_1_out, WE, RST);
  Demultiplexer #(.select(3)) demultiplexer_1 (
    .out0(demultiplexer_1_out0), .out1(demultiplexer_1_out1), .out2(demultiplexer_1_out2),
    .out3(demultiplexer_1_out3), .out4(demultiplexer_1_out4), .out5(demultiplexer_1_out5),
    .out7(demultiplexer_1_out7), .in(or_1_out), .sel(REG_WRITE));  // open: out6
  Register R1 (.D(INP), .en(demultiplexer_1_out1), .clk(CLK), .Q(SCREEN_Y), .clr(RST));
  Register R2 (.D(INP), .en(demultiplexer_1_out2), .clk(CLK), .Q(IO_R2), .clr(RST));
  Register R3 (.D(INP), .en(demultiplexer_1_out3), .clk(CLK), .Q(IO_R3), .clr(RST));
  Register R4 (.D(INP), .en(demultiplexer_1_out4), .clk(CLK), .Q(IO_R4), .clr(RST));
  Register R5 (.D(INP), .en(demultiplexer_1_out5), .clk(CLK), .Q(INSTR_PAGE), .clr(RST));
  Register R6 (.D(INP_KEYBOARD), .en(WE_KEYBOARD), .clk(CLK), .Q(KEYBOARD), .clr(RST));
  Register R7 (.D(INP), .en(demultiplexer_1_out7), .clk(CLK), .Q(IO_R7), .clr(RST));
  Counter ScreenX (
    .load(demultiplexer_1_out0), .D(INP), .count(DO_PC_INCREMENT), .Q(SCREEN_X), .up(1'b1), .clk(CLK),
    .clr(RST));  // open: carry
  Multiplexer #(.select(3), .width(8)) multiplexer_1 (
    .in0(SCREEN_X), .in1(SCREEN_Y), .in2(IO_R2), .in3(IO_R3), .in4(IO_R4), .in5(INSTR_PAGE), .in6(KEYBOARD),
    .in7(IO_R7), .out(OUT_A), .sel(REG_READ_A));

  // Notes on the sheet:
  //   REG_WRITE: initial=0x2
endmodule
