// Logisim project MPMPcpu_phase3_data_attempt.circ as structural Verilog
module main (
  input  in_1
);

  wire and_2_out, and_5_out, and_6_out, and_7_out, c1, c2, c3, c4, CLK, CTRL_ALU_Y_USE_IMM,
       CTRL_RAM_ADDR_SRC, CTRL_RAM_WE, CTRL_REG_A_IS_REG_RES, CTRL_RF_INP_USE_IO, CTRL_RF_INP_USE_MEM,
       CTRL_RF_WE, CTRL_ZERO_MASK_ALU_OUT_A, IO_WE, IS_DATA, IS_RI, IS_RRI, IS_RRR, not_1_out, or_1_out;
  wire [1:0] CYCLE;
  wire [2:0] REG_A, REG_B, REG_RES;
  wire [3:0] and_10_out, multiplexer_6_out, OP4;
  wire [3:3] not_3_out;
  wire [7:0] alu_1_result, alu_1_zf, FLAGS_q, IMM, INSTR_ADDR, INSTR_PAGE, IO_ADDR, IO_READ_VAL,
       multiplexer_1_out, multiplexer_2_out, RAM_ADDR, RAM_INP, RAM_OUT, registerfile_1_dbg_r2,
       registerfile_1_dbg_r3, registerfile_1_dbg_r4, registerfile_1_dbg_r5, registerfile_1_dbg_r6,
       registerfile_1_dbg_r7, registerfile_1_out_a, registerfile_1_out_b, registerfile_1_sp, undriven,
       undriven_2, undriven_3, undriven_4;
  wire [7:3] dipswitch_1_sw13;
  wire [7:6] not_2_out;
  wire [15:0] register_1_q, rom_1_data;

  RAM ram_1 (.addr(RAM_ADDR), .we(CTRL_RAM_WE), .oe(1'b1), .clk(CLK), .din(RAM_INP), .dout(RAM_OUT));
  ROM #(.addrWidth(16), .dataWidth(16)) rom_1 (.addr({INSTR_PAGE, INSTR_ADDR}), .data(rom_1_data));
  Multiplexer #(.width(8)) multiplexer_1 (
    .in0(RAM_INP), .in1(RAM_OUT), .out(multiplexer_1_out), .sel(CTRL_RF_INP_USE_MEM));
  // Probe on RAM_INP
  Multiplexer #(.width(8)) multiplexer_2 (
    .in0(multiplexer_1_out), .in1(IO_READ_VAL), .out(multiplexer_2_out), .sel(CTRL_RF_INP_USE_IO));
  DipSwitch #(.number(16)) dipswitch_1 (
    .sw1(OP4[3]), .sw2(OP4[2]), .sw3(OP4[1]), .sw4(OP4[0]), .sw5(IS_RI), .sw6(REG_RES[2]), .sw7(REG_RES[1]),
    .sw8(REG_RES[0]), .sw9(dipswitch_1_sw13[7]), .sw10(dipswitch_1_sw13[6]), .sw11(dipswitch_1_sw13[5]),
    .sw12(dipswitch_1_sw13[4]), .sw13(dipswitch_1_sw13[3]), .sw14(REG_B[2]), .sw15(REG_B[1]), .sw16(REG_B[0]));
  // Probe on multiplexer_2_out
  Register #(.width(16)) register_1 (.D(rom_1_data), .en(c1), .clk(CLK), .Q(register_1_q), .clr(in_1));
  Multiplexer #(.width(3)) multiplexer_3 (.in0(REG_RES), .in1(dipswitch_1_sw13[5:3]), .out(REG_A), .sel(not_1_out));
  not not_1 (not_1_out, CTRL_REG_A_IS_REG_RES);
  and and_1 (IS_RRR, and_2_out, ~IS_RI);  // AND_Gate
  and and_2 (and_2_out, dipswitch_1_sw13[7], ~dipswitch_1_sw13[6]);  // AND_Gate
  RegisterFile registerfile_1 (
    .CLK(CLK), .RST(in_1), .DO_PC_INCREMENT(c3), .INP(multiplexer_2_out), .REG_WRITE(REG_RES),
    .REG_READ_A(REG_A), .ZERO_MASK_OUT_A(CTRL_ZERO_MASK_ALU_OUT_A), .WE(CTRL_RF_WE), .REG_READ_B(REG_B),
    .PC(INSTR_ADDR), .OUT_A(registerfile_1_out_a), .SP(registerfile_1_sp), .OUT_B(registerfile_1_out_b),
    .DBG_R2(registerfile_1_dbg_r2), .DBG_R3(registerfile_1_dbg_r3), .DBG_R4(registerfile_1_dbg_r4),
    .DBG_R5(registerfile_1_dbg_r5), .DBG_R6(registerfile_1_dbg_r6), .DBG_R7(registerfile_1_dbg_r7));
  and and_3 (IS_RRI, and_5_out, ~IS_RI);  // AND_Gate
  and and_4 (IS_DATA, and_6_out, ~IS_RI);  // AND_Gate
  and and_5 (and_5_out, dipswitch_1_sw13[7], dipswitch_1_sw13[6]);
  and and_6 (and_6_out, ~dipswitch_1_sw13[7], ~dipswitch_1_sw13[6]);  // AND_Gate
  // Probe on INSTR_ADDR
  // Probe on registerfile_1_sp
  // Probe on registerfile_1_dbg_r2
  // Probe on registerfile_1_dbg_r3
  // Probe on registerfile_1_dbg_r4
  // Probe on registerfile_1_dbg_r5
  // Probe on registerfile_1_dbg_r6
  // Probe on registerfile_1_dbg_r7
  or or_1 (or_1_out, IS_RI, and_7_out);
  and and_7 (and_7_out, ~IS_RI, dipswitch_1_sw13[7]);  // AND_Gate
  and and_8 (not_2_out[7], ~IS_RI, dipswitch_1_sw13[6]);  // AND_Gate
  assign IMM = {dipswitch_1_sw13, REG_B} & {{5{IS_RI}}, 3'b111};  // AND_Gate and_9, 8 bits wide
  // Probe on IMM
  // Probe on registerfile_1_out_a
  Multiplexer #(.width(8)) multiplexer_4 (
    .in0(registerfile_1_out_b), .in1(IMM), .out(IO_ADDR), .sel(CTRL_ALU_Y_USE_IMM));
  not not_2 (not_2_out[6], or_1_out);
  ROM CONTROL_ROM (.addr({not_2_out, OP4, CYCLE}));  // open: data
  not not_3 (not_3_out[3], IS_RI);
  // Probe on and_10_out
  assign and_10_out = {4{not_3_out[3]}} & OP4;  // AND_Gate and_10, 4 bits wide
  // Probe on IO_ADDR
  Multiplexer #(.width(8)) multiplexer_5 (
    .in0(registerfile_1_out_a), .in1(IO_ADDR), .out(RAM_ADDR), .sel(CTRL_RAM_ADDR_SRC));
  Demultiplexer #(.select(2)) demultiplexer_1 (.out0(c1), .out1(c2), .out2(c3), .out3(c4), .in(1'b1), .sel(CYCLE));
  Counter #(.max('h3), .width(2)) counter_1 (
    .load(1'b0), .count(1'b1), .Q(CYCLE), .up(1'b1), .clk(CLK), .clr(in_1));  // open: D, carry
  Clock clock_1 (.out(CLK));
  // DipSwitch dipswitch_2: pin names not known
  // Probe on undriven
  ALU alu_1 (
    .OP(and_10_out), .X(registerfile_1_out_a), .Y(IO_ADDR), .CIN(FLAGS_q[0]), .ZF(alu_1_zf[0]),
    .RESULT(alu_1_result), .OVF(alu_1_zf[1]));  // open: EF, RF, CF
  // DipSwitch dipswitch_3: pin names not known
  // Probe on undriven_2
  RegisterFile registerfile_2 (
    .CLK(CLK), .RST(in_1), .DO_PC_INCREMENT(1'b0), .INP(registerfile_1_out_a), .REG_WRITE(IO_ADDR[2:0]),
    .REG_READ_A(IO_ADDR[2:0]), .ZERO_MASK_OUT_A(1'b0), .WE(IO_WE), .OUT_A(IO_READ_VAL), .DBG_R5(INSTR_PAGE));  // open: REG_READ_B, PC, SP, OUT_B, DBG_R2, DBG_R3, DBG_R4, DBG_R6, DBG_R7
  // Probe on alu_1_result
  Register ALU_RESULT (.D(alu_1_result), .en(c2), .clk(CLK), .Q(RAM_INP), .clr(in_1));
  Register FLAGS (.D(alu_1_zf), .en(c2), .clk(CLK), .Q(FLAGS_q), .clr(in_1));
  // DipSwitch dipswitch_4: pin names not known
  // DipSwitch dipswitch_5: pin names not known; wires that end beside it: CTRL_RF_INP_USE_MEM
  // Probe on undriven_3
  // Probe on undriven_4
  Multiplexer #(.select(2), .width(8)) multiplexer_6 (
    .in0(undriven), .in1(undriven_2), .in2(undriven_3), .in3(undriven_4),
    .out({CTRL_ZERO_MASK_ALU_OUT_A, CTRL_ALU_Y_USE_IMM, CTRL_RF_INP_USE_IO, CTRL_RF_INP_USE_MEM, multiplexer_6_out}),
    .sel(CYCLE));
  Demultiplexer #(.select(2)) demultiplexer_2 (
    .out1(CTRL_RF_WE), .out2(CTRL_RAM_WE), .out3(IO_WE), .in(1'b1), .sel(multiplexer_6_out[1:0]));  // open: out0

  // Other names for the same wires on the sheet: CTRL_CW_WE = c1; CTRL_ALU_WE = c2; CTRL_INCREMENT_PC = c3;
  //   RST = in_1

  // Notes on the sheet:
  //   Data Memory
  //   Instruction Memory
  //   12      8      4      0
  //   ███████████████
  //   TODO: Check if we can squash the 4 input sources (mem, io, OUT_B, IMM) into a 2-bit select encoder to save bits in control bit memory
  //   contents of CONTROL_ROM (hex, n*v repeats v):
  //   53*0 a4 0 0 0 31 0 0 0 20 1
  //   Control Bit Memory
  //   TODO: Do Write in Fixed Cycle (ala v. Neumann) and move 3 first control bits into 2 bits
endmodule

module ALU (
  input  [3:0] OP,
  input  [7:0] X,
  input  [7:0] Y,
  input  CIN,
  output ZF,
  output [7:0] RESULT,
  output OVF,
  output EF,
  output RF,
  output CF
);

  wire ADD_COUT, and_1_out, and_4_out, and_5_out, bitfinder_1_found, bitfinder_2_found, C_OP,
       comparator_1_eq, comparator_2_lt, comparator_3_lt, comparator_4_eq, comparator_5_eq, comparator_6_eq,
       comparator_7_gt, not_2_out, SUB_COUT;
  wire [2:0] bitfinder_1_index, bitfinder_2_index, multiplexer_3_out, subtractor_2_out;
  wire [2:2] not_3_out;
  wire [7:0] adder_1_out, and_2_out, DIV_REM, divider_1_out, MUL_CARRY, multiplier_1_out, negator_1_out,
       not_1_out, or_1_out, shifter_1_out, shifter_2_out, subtractor_1_out, xnor_1_out, xor_1_out;

  and and_1 (and_1_out, CIN, C_OP);
  Adder adder_1 (.a(X), .b(Y), .out(adder_1_out), .cin(and_1_out), .cout(ADD_COUT));
  Subtractor subtractor_1 (.a(X), .b(Y), .out(subtractor_1_out), .bin(and_1_out), .bout(SUB_COUT));
  Multiplier multiplier_1 (.a(X), .b(Y), .out(multiplier_1_out), .cout(MUL_CARRY));  // open: cin
  Divider divider_1 (.a(X), .b(Y), .out(divider_1_out), .rem(DIV_REM));  // open: upper
  Shifter shifter_1 (.in(X), .\dist (Y[2:0]), .out(shifter_1_out));
  Shifter #(.shift("lr")) shifter_2 (.in(X), .\dist (Y[2:0]), .out(shifter_2_out));
  Negator negator_1 (.in(X), .out(negator_1_out));
  assign and_2_out = X & Y;  // AND_Gate and_2, 8 bits wide
  assign or_1_out = X | Y;  // OR_Gate or_1, 8 bits wide
  assign xor_1_out = X ^ Y;  // XOR_Gate xor_1, 8 bits wide
  assign xnor_1_out = ~(X ^ Y);  // XNOR_Gate xnor_1, 8 bits wide
  assign not_1_out = ~X;  // NOT_Gate not_1, 8 bits wide
  and and_3 (C_OP, OP[1], OP[2], OP[3]);
  Multiplexer #(.select(4), .width(8)) multiplexer_1 (
    .in0(adder_1_out), .in1(subtractor_1_out), .in2(multiplier_1_out), .in3(divider_1_out),
    .in4(shifter_1_out), .in5(shifter_2_out), .in6(negator_1_out), .in7(X), .in8(Y), .in9(and_2_out),
    .in10(or_1_out), .in11(xor_1_out), .in12(xnor_1_out), .in13(not_1_out), .in14(adder_1_out),
    .in15(subtractor_1_out), .out(RESULT), .sel(OP));
  BitFinder #(.\type ("high1")) bitfinder_1 (.in(X), .index(bitfinder_1_index), .found(bitfinder_1_found));
  BitFinder bitfinder_2 (.in(X), .index(bitfinder_2_index), .found(bitfinder_2_found));
  nor Zero_Test (ZF, RESULT[7], RESULT[6], RESULT[5], RESULT[4], RESULT[3], RESULT[2], RESULT[1], RESULT[0]);
  Subtractor #(.width(3)) subtractor_2 (.a(3'b111), .b(bitfinder_1_index), .out(subtractor_2_out));  // open: bin, bout
  Comparator #(.mode("unsigned"), .width(4)) comparator_1 (.a(OP), .b(4'b0011), .eq(comparator_1_eq));  // open: gt, lt
  Comparator #(.mode("unsigned"), .width(3)) comparator_2 (
    .a(subtractor_2_out), .b(Y[2:0]), .lt(comparator_2_lt));  // open: gt, eq
  and and_4 (and_4_out, comparator_2_lt, bitfinder_1_found);
  Comparator #(.mode("unsigned"), .width(3)) comparator_3 (
    .a(bitfinder_2_index), .b(Y[2:0]), .lt(comparator_3_lt));  // open: gt, eq
  and and_5 (and_5_out, comparator_3_lt, bitfinder_2_found);
  Comparator #(.mode("unsigned")) comparator_4 (.a(Y), .b({8{1'b0}}), .eq(comparator_4_eq));  // open: gt, lt
  Comparator #(.mode("unsigned")) comparator_5 (.a(DIV_REM), .b({8{1'b0}}), .eq(comparator_5_eq));  // open: gt, lt
  Comparator #(.mode("unsigned"), .width(4)) comparator_6 (.a(OP), .b(4'b0010), .eq(comparator_6_eq));  // open: gt, lt
  and and_6 (OVF, comparator_6_eq, comparator_7_gt);
  Comparator #(.mode("unsigned")) comparator_7 (.a(MUL_CARRY), .b({8{1'b0}}), .gt(comparator_7_gt));  // open: eq, lt
  and and_7 (EF, comparator_4_eq, comparator_1_eq);
  and and_8 (RF, comparator_1_eq, not_2_out);
  not not_2 (not_2_out, comparator_5_eq);
  Multiplexer #(.select(3)) multiplexer_2 (
    .in0(ADD_COUT), .in1(SUB_COUT), .in4(and_4_out), .in5(and_5_out), .out(CF), .sel(multiplexer_3_out));  // open: in2, in3, in6, in7
  Multiplexer #(.width(3)) multiplexer_3 (
    .in0(OP[2:0]), .in1({not_3_out[2], 2'b00}), .out(multiplexer_3_out), .sel(C_OP));
  not not_3 (not_3_out[2], OP[0]);

  // Other names for the same wires on the sheet: SHIFT[2:0] = Y[2:0]

  // Notes on the sheet:
  //   TODO: Overflow Flag for Add, Sub, AddC, SubC
endmodule

module RegisterFile (
  input  CLK,
  input  RST,
  input  DO_PC_INCREMENT,
  input  [7:0] INP,
  input  [2:0] REG_WRITE,
  input  [2:0] REG_READ_A,
  input  ZERO_MASK_OUT_A,
  input  WE,
  input  [2:0] REG_READ_B,
  output [7:0] PC,
  output [7:0] OUT_A,
  output [7:0] SP,
  output [7:0] OUT_B,
  output [7:0] DBG_R2,
  output [7:0] DBG_R3,
  output [7:0] DBG_R4,
  output [7:0] DBG_R5,
  output [7:0] DBG_R6,
  output [7:0] DBG_R7
);

  wire and_1_out, comparator_1_lt, demultiplexer_1_out0, demultiplexer_1_out1, demultiplexer_1_out2,
       demultiplexer_1_out3, demultiplexer_1_out4, demultiplexer_1_out5, demultiplexer_1_out6,
       demultiplexer_1_out7, or_1_out;
  wire [2:0] multiplexer_2_out;
  wire [7:0] INP_t, multiplexer_3_out;

  Multiplexer #(.width(8)) multiplexer_1 (.in0(INP), .in1({8{1'b1}}), .out(INP_t), .sel(RST));
  Multiplexer #(.width(3)) multiplexer_2 (.in0(REG_WRITE), .in1(3'b010), .out(multiplexer_2_out), .sel(RST));
  or or_1 (or_1_out, WE, RST);
  Demultiplexer #(.select(3)) demultiplexer_1 (
    .out0(demultiplexer_1_out0), .out1(demultiplexer_1_out1), .out2(demultiplexer_1_out2),
    .out3(demultiplexer_1_out3), .out4(demultiplexer_1_out4), .out5(demultiplexer_1_out5),
    .out6(demultiplexer_1_out6), .out7(demultiplexer_1_out7), .in(or_1_out), .sel(multiplexer_2_out));
  Comparator #(.mode("unsigned"), .width(3)) comparator_1 (
    .a(3'b000), .b(REG_WRITE), .lt(comparator_1_lt));  // open: gt, eq
  and and_1 (and_1_out, comparator_1_lt, DO_PC_INCREMENT);
  Register R1 (.D(INP_t), .en(demultiplexer_1_out1), .clk(CLK), .Q(SP), .clr(RST));
  Register R2 (.D(INP_t), .en(demultiplexer_1_out2), .clk(CLK), .Q(DBG_R2));  // open: clr
  Register R3 (.D(INP_t), .en(demultiplexer_1_out3), .clk(CLK), .Q(DBG_R3), .clr(RST));
  Register R4 (.D(INP_t), .en(demultiplexer_1_out4), .clk(CLK), .Q(DBG_R4), .clr(RST));
  Register R5 (.D(INP_t), .en(demultiplexer_1_out5), .clk(CLK), .Q(DBG_R5), .clr(RST));
  Register R6 (.D(INP_t), .en(demultiplexer_1_out6), .clk(CLK), .Q(DBG_R6), .clr(RST));
  Register R7 (.D(INP_t), .en(demultiplexer_1_out7), .clk(CLK), .Q(DBG_R7), .clr(RST));
  Counter ProgramCounter (
    .load(demultiplexer_1_out0), .D(INP_t), .count(and_1_out), .Q(PC), .up(1'b1), .clk(CLK), .clr(RST));  // open: carry
  Multiplexer #(.select(3), .width(8)) multiplexer_3 (
    .in0(PC), .in1(SP), .in2(DBG_R2), .in3(DBG_R3), .in4(DBG_R4), .in5(DBG_R5), .in6(DBG_R6), .in7(DBG_R7),
    .out(multiplexer_3_out), .sel(REG_READ_A));
  Multiplexer #(.select(3), .width(8)) multiplexer_4 (
    .in0(PC), .in1(SP), .in2(DBG_R2), .in3(DBG_R3), .in4(DBG_R4), .in5(DBG_R5), .in6(DBG_R6), .in7(DBG_R7),
    .out(OUT_B), .sel(REG_READ_B));
  Multiplexer #(.width(8)) multiplexer_5 (.in0(multiplexer_3_out), .in1({8{1'b0}}), .out(OUT_A), .sel(ZERO_MASK_OUT_A));

  // Notes on the sheet:
  //   REG_WRITE: initial=0x2
endmodule
